# Fritzing sketch Ceed_Schematic (saved by Fritzing 0.9.3b)
breadboards: 1

parts:
  Raspberry_Pi_1 = Raspberry Pi 3 [part_number=RPI-3-V1.2]
  hc-sr1 = hc-sr04
  S7 = Round Pushbutton
  S8 = Round Pushbutton  # not connected
  S9 = Round Pushbutton
  S10 = Round Pushbutton
  S11 = Round Pushbutton
  S12 = Round Pushbutton
  R1 = Resistor [tolerance=±5% resistance=220 package=THT]
  R2 = Resistor [tolerance=±5% resistance=220 package=THT]

nets:
  N1: Raspberry_Pi_1.GPIO4, hc-sr1.Trig
  GND: Raspberry_Pi_1.GND, hc-sr1.GND, S7.leg1, S9.leg1, S10.leg1, S11.leg0, S12.leg0, R2.Pin_1
  N2: Raspberry_Pi_1.GPIO17, R1.Pin_1, R2.Pin_0
  N3: Raspberry_Pi_1.GPIO19, S9.leg0
  N4: Raspberry_Pi_1.GPIO21, S7.leg0
  N5: Raspberry_Pi_1.GPIO12, S10.leg0
  N6: Raspberry_Pi_1.GPIO15, S12.leg1
  N7: Raspberry_Pi_1.GPIO14, S11.leg1
  5V: Raspberry_Pi_1.5V, hc-sr1.VCC
